# Fritzing sketch schema (saved by Fritzing 0.8.7b)

parts:
  Composant1 = Arduino Pro Mini v13
  BREAKOUT1 = HMC5883L Compass Breakout

nets:
  N1: Composant1.A4, BREAKOUT1.SDA
  N2: Composant1.A5, BREAKOUT1.SCL
  GND: Composant1.GND, BREAKOUT1.GND
  VCC: Composant1.VCC, BREAKOUT1.VIN
