# Fritzing sketch Schema (saved by Fritzing 0.8.7b)

parts:
  PIR1 = PIR sensor
  Composant1 = Arduino Uno (Rev3)

nets:
  VDD: PIR1.VDD, Composant1.5V
  N1: PIR1.SIG, Composant1.D2
  GND: PIR1.GND, Composant1.GND
