# Fritzing sketch schema (saved by Fritzing 0.8.7b)

parts:
  GY1 = MPU-6050 Board GY-521 [form="♀ (female)" package=THT]
  Composant1 = Arduino Pro Mini v13

nets:
  N1: GY1.pin1, Composant1.VCC
  N2: GY1.pin2, Composant1.GND
  N3: GY1.pin3, Composant1.A5
  N4: GY1.pin4, Composant1.A4
  N5: GY1.pin8, Composant1.D2

custom parts:
  MPU-6050 Board GY-521: Acelerometro y Giroscopio MPU-6050 Board GY-521
