# Fritzing sketch schema (saved by Fritzing 0.8.7b)

parts:
  DHT1 = DHT11 Humitidy and Temperature Sensor
  Composant1 = Arduino Uno (Rev3)
  R1 = Resistor [tolerance=±5% resistance=1k package=THT]

nets:
  VDD: DHT1.VDD, Composant1.5V
  N1: DHT1.DATA, Composant1.D2, R1.Pin_1
  GND: DHT1.GND, Composant1.GND

custom parts:
  DHT11 Humitidy and Temperature Sensor: DHT11 Humidity and Temperature Sensor
