# Fritzing sketch schema (saved by Fritzing 0.8.7b)

parts:
  Composant1 = SRF05 Ultrasonic Rangefinder
  Composant2 = Arduino Pro Mini v13

nets:
  VCC: Composant1.VCC, Composant2.VCC
  N1: Composant1.Trig, Composant2.D11_PWM/MOSI
  N2: Composant1.Echo, Composant2.D10_PWM/SS
  GND: Composant1.GND, Composant2.GND
