# Fritzing sketch schema (saved by Fritzing 0.8.7b)

parts:
  Composant3 = Arduino Uno (Rev3)
  S1 = Pushbutton [package="[THT]"]
  R1 = Resistor [tolerance=±5% resistance=220 package=THT]
  R2 = Resistor [tolerance=±5% resistance=220 package=THT]
  LED1 = LED - 5mm [color="Red (633nm)" package="5 mm [THT]"]

nets:
  N1: Composant3.D13/SCK, R2.Pin_1
  N2: Composant3.GND, R1.Pin_0, LED1.cathode
  N3: Composant3.D3_PWM, S1.Pin_3, S1.Pin_4, R1.Pin_1
  N4: Composant3.5V, S1.Pin_2
  N5: R2.Pin_0, LED1.anode
